# Fritzing sketch SCHEMA_COMPLETA_CONEXIUNI_FRITZING (saved by Fritzing 0.9.5d)
breadboards: 1

parts:
  esp1 = ESP32 DevKitc V4
  OLED_I2C1 = OLED 128x64 I2C Monochrome Display
  ZS-042_RTC2 = ZS-042 RTC Module
  R1 = Photocell (LDR) [package=THT]
  R2 = Resistor [tolerance=±5% resistance=10k package="2010 [SMD]"]
  YL-83_-_Detection_Board1 = YL-83 Rain Sensor - Detection Board
  YL-83_-_Control_Board2 = YL-83 Rain Sensor - Control Board
  M1 = BME280
  Parte3 = LED Tactile Button Breakout v10 [part_number=BOB-10467]
  LCD1 = LCD screen

nets:
  N1: esp1.IO4, Parte3.2
  N2: esp1.GND#12, Parte3.1
  N3: esp1.IO22, OLED_I2C1.SCK, ZS-042_RTC2.SCL, M1.SCL
  VDD: esp1.3V3, OLED_I2C1.VDD, R1.pin_0, YL-83_-_Control_Board2.VCC, M1.VIN, LCD1.VDD, LCD1.LED+
  N4: esp1.IO34, R1.pin_1, R2.Pin_0
  N5: esp1.IO35, YL-83_-_Control_Board2.AO
  N6: esp1.IO32, LCD1.DB6
  N7: esp1.IO33, LCD1.DB7
  N8: esp1.IO25, LCD1.RS
  N9: esp1.IO26, LCD1.E
  N10: esp1.IO27, LCD1.DB5
  N11: esp1.IO14, LCD1.DB4
  GND: esp1.GND#32, OLED_I2C1.GND, R2.Pin_1, YL-83_-_Control_Board2.GND, M1.GND, LCD1.VSS, LCD1.V0, LCD1.R/W, LCD1.LED-
  N12: OLED_I2C1.SDA, M1.SDA
  N13: YL-83_-_Detection_Board1.POS, YL-83_-_Control_Board2.POS
  N14: YL-83_-_Detection_Board1.NEG, YL-83_-_Control_Board2.NEG

custom parts:
  ESP32 DevKitc V4: ESP32-DevKitC board with ESP32-WROOM-32 module. ESP32-DevKitC V4 is a small-sized ESP32-based development board produced by Espressif. Most of the pins on the ESP module are broken out to the pin headers on the board. The pins D0, D1, D2, D3, CMD and CLK are used internally for communication between ESP32 and SPI flash memory. They are grouped on both sides near the USB connector. Avoid using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
  YL-83 Rain Sensor - Detection Board: The YL-83 is a rain sensor that has more resistance when dry and less resistance when wet. The module runs at 5V.
  YL-83 Rain Sensor - Control Board: The YL-83 is a rain sensor that has more resistance when dry and less resistance when wet. The module runs at 5V.
  BME280: Temperature Humidity Barometric presure Sensor

// code stored in the sketch: Untitled2.ino
#include <Wire.h>
#include <Adafruit_SSD1306.h>
#include <Adafruit_GFX.h>
#include <LiquidCrystal.h>
#include <RTClib.h>
#include <Adafruit_BME280.h>

// --- OLED 128x64 ---
#define SCREEN_WIDTH 128
#define SCREEN_HEIGHT 64
Adafruit_SSD1306 display(SCREEN_WIDTH, SCREEN_HEIGHT, &Wire, -1);

// --- LCD 1602 ---
LiquidCrystal lcd(25, 26, 14, 27, 32, 33);  // RS, E, D4, D5, D6, D7

// --- RTC ---
RTC_DS3231 rtc;

// --- Senzori ---
Adafruit_BME280 bme;  // I2C: SDA=21, SCL=22
const int senzorPloaie = 35;  // analog input
const int pragPloaie = 2000;  // prag ud/uscat

void setup() {
  Wire.begin();
  Serial.begin(115200);

  // Init OLED
  display.begin(SSD1306_SWITCHCAPVCC, 0x3C);
  display.clearDisplay();

  // Init LCD
  lcd.begin(16, 2);
  lcd.setCursor(0, 0);
  lcd.print("STATIE METEO");

  // Init RTC
  rtc.begin();
  if (rtc.lostPower()) {
    rtc.adjust(DateTime(F(__DATE__), F(__TIME__))); // sincronizare initiala
  }

  // Init BME280
  if (!bme.begin(0x76)) {
    Serial.println("Eroare BME280!");
    while (1);
  }

  pinMode(senzorPloaie, INPUT);
}

void loop() {
  DateTime now = rtc.now();
  int valoarePloaie = analogRead(senzorPloaie);

  float temp = bme.readTemperature();
  float hum = bme.readHumidity();

  // --- Afi?aj OLED ---
  display.clearDisplay();
  display.setTextSize(1);
  display.setTextColor(WHITE);

  display.setCursor(0, 0);
  display.print("Temp: ");
  display.print(temp);
  display.println(" C");

  display.setCursor(0, 15);
  display.print("Umid: ");
  display.print(hum);
  display.println(" %");

  display.setCursor(0, 30);
  if (valoarePloaie < pragPloaie) {
    display.println("PLOUA");
  } else {
    display.println("NU PLOUA");
  }

  display.display();

  // --- Afi?aj LCD ---
  lcd.setCursor(0, 1);
  lcd.print("D:");
  if (now.day() < 10) lcd.print('0');
  lcd.print(now.day());
  lcd.print('/');
  if (now.month() < 10) lcd.print('0');
  lcd.print(now.month());

  lcd.print(" T:");
  if (now.hour() < 10) lcd.print('0');
  lcd.print(now.hour());
  lcd.print(':');
  if (now.minute() < 10) lcd.print('0');
  lcd.print(now.minute());

  delay(1000);
}
